// Logisim project 150115006_150118509_150115851.circ as structural Verilog: 18 circuits, main circuit main
module main (
  input  reset
);

  wire branchResult, Clock, isBranch, isImmediate, isInstructionWritable, isJump, isLoad, isPCWritable,
       isRegisterWritable, isStore, or_1_out, or_2_out;
  wire [1:0] ALU_Selection;
  wire [3:0] dstAddr, multiplexer_2_out, multiplexer_3_out, src1Addr, src2Addr;
  wire [5:0] branchAddress, immediateValue;
  wire [9:0] loadAddress, program_counter_1_instructionaddress;
  wire [13:0] jumpAddress;
  wire [17:0] ALUResult, instruction, memoryData, multiplexer_1_out, multiplexer_4_out,
       n6x18bits_extension_1_output, op1In, op2In, rom_1_data, scr2Out;

  Clock clock_1 (.out(Clock));
  Multiplexer #(.width(18), .enable("false")) multiplexer_1 (
    .in0(scr2Out), .in1(n6x18bits_extension_1_output), .out(multiplexer_1_out), .sel(isImmediate));
  Arithmetic_Logic_Unit arithmetic_logic_unit_1 (.r(ALUResult), .a(op1In), .b(multiplexer_1_out), .s(ALU_Selection));
  // Probe on program_counter_1_instructionaddress
  Program_Counter program_counter_1 (
    .jumpAddr(jumpAddress), .branchAddr(branchAddress), .isJump(isJump), .isBranch(branchResult),
    .instructionAddress(program_counter_1_instructionaddress), .write_enabled(isPCWritable), .clk(Clock),
    .rst(reset));
  _6x18Bits_Extension u_6x18bits_extension_1 (
    .\output (n6x18bits_extension_1_output), .\input (immediateValue), .in_2(1'b1));
  ROM #(.addrWidth(10), .dataWidth(18)) rom_1 (
    .addr(program_counter_1_instructionaddress), .data(rom_1_data));  // open: sel
  Bit_Extender #(.in_width(6), .out_width(18), .\type ("sign")) bit_extender_1 ();  // open: in, out
  or or_1 (or_1_out, isStore, isBranch);
  // Probe on rom_1_data
  Register #(.width(18)) register_1 (
    .D(rom_1_data), .en(isInstructionWritable), .Q(instruction), .clk(Clock));  // open: clr
  Multiplexer #(.width(4), .enable("false")) multiplexer_2 (
    .in0(src1Addr), .in1(dstAddr), .out(multiplexer_2_out), .sel(or_1_out));
  // Probe on instruction
  Multiplexer #(.width(4), .enable("false")) multiplexer_3 (
    .in0(src2Addr), .in1(src1Addr), .out(multiplexer_3_out), .sel(isBranch));
  Multiplexer #(.width(18), .enable("false")) multiplexer_4 (
    .in0(ALUResult), .in1(memoryData), .out(multiplexer_4_out), .sel(or_2_out));
  or or_2 (or_2_out, isStore, isLoad);
  _18_Bits_Register_File u_18_bits_register_file_1 (
    .\input (multiplexer_4_out), .dstaddr(dstAddr), .src1adr(multiplexer_2_out), .src2Adr(multiplexer_3_out),
    .clk(Clock), .load(isRegisterWritable), .src1_out(op1In), .src2_out(op2In));  // open: rst
  // Probe on dstAddr
  Control_Unit control_unit_1 (
    .Instruction(instruction), .dstAddr(dstAddr), .src1Addr(src1Addr), .src2Addr(src2Addr),
    .loadAddrress(loadAddress), .jumpAddrress(jumpAddress), .branchAddress(branchAddress),
    .immValue(immediateValue), .isImmediate(isImmediate), .isRegisterWritable(isRegisterWritable),
    .isJump(isJump), .isLoad(isLoad), .isStore(isStore), .clk(Clock), .opInput1(op1In), .opIntput2(op2In),
    .branchSignal(branchResult), .isBranch(isBranch), .IRW(isInstructionWritable), .PCW(isPCWritable),
    .ALUSelectionBits(ALU_Selection));
  // Probe on src1Addr
  RAM #(.addrWidth(10), .dataWidth(18), .bus("separate")) ram_1 (
    .addr(loadAddress), .din(op1In), .data(memoryData), .str(isStore), .clk(Clock), .ld(isLoad));  // open: sel, clr
  // Probe on src2Addr

  // Other names for the same wires on the sheet: src1Out[17:0] = op1In; src2Out[17:0] = op2In

  // Notes on the sheet:
  //   contents of rom_1 (hex, n*v repeats v):
  //   4416 480a 4c0d 6414 28c03 25003 5109 5500 447f 3886e 2940d 25c03 5dc6 61c0 4441 36469 20003 2884
  //   20006 6c94 7095 7496 7897 23ffa
endmodule

module _18_Bits_Register_File (
  input  [17:0] \input ,
  input  [3:0] dstaddr,
  input  [3:0] src1adr,
  input  [3:0] src2Adr,
  input  clk,
  input  load,
  input  rst,
  output [17:0] src1_out,
  output [17:0] src2_out
);

  wire decoder_2_out0, decoder_2_out1, decoder_2_out2, decoder_2_out3, decoder_2_out4, decoder_2_out5,
       decoder_2_out6, decoder_2_out7, decoder_2_out8, decoder_2_out9, decoder_2_out10, decoder_2_out11,
       decoder_2_out12, decoder_2_out13, decoder_2_out14, decoder_2_out15, decoder_3_out0, decoder_3_out1,
       decoder_3_out2, decoder_3_out3, decoder_3_out4, decoder_3_out5, decoder_3_out6, decoder_3_out7,
       decoder_3_out8, decoder_3_out9, decoder_3_out10, decoder_3_out11, decoder_3_out12, decoder_3_out13,
       decoder_3_out14, decoder_3_out15, r0, r1, r2, r3, r4, r5, r6, r7, r8, r9, r10, r11, r12, r13, r14, r15;
  wire [17:0] register_1_q, register_2_q, register_3_q, register_4_q, register_5_q, register_6_q,
       register_7_q, register_8_q, register_9_q, register_10_q, register_11_q, register_12_q, register_13_q,
       register_14_q, register_15_q, register_16_q;

  Decoder #(.select(4)) decoder_1 (
    .out0(r0), .out1(r1), .out2(r2), .out3(r3), .out4(r4), .out5(r5), .out6(r6), .out7(r7), .out8(r8),
    .out9(r9), .out10(r10), .out11(r11), .out12(r12), .out13(r13), .out14(r14), .out15(r15), .sel(dstaddr),
    .en(load));
  Decoder #(.select(4), .enable("false")) decoder_2 (
    .out0(decoder_2_out0), .out1(decoder_2_out1), .out2(decoder_2_out2), .out3(decoder_2_out3),
    .out4(decoder_2_out4), .out5(decoder_2_out5), .out6(decoder_2_out6), .out7(decoder_2_out7),
    .out8(decoder_2_out8), .out9(decoder_2_out9), .out10(decoder_2_out10), .out11(decoder_2_out11),
    .out12(decoder_2_out12), .out13(decoder_2_out13), .out14(decoder_2_out14), .out15(decoder_2_out15),
    .sel(src1adr));
  Register #(.width(18)) register_1 (.D(\input ), .en(r1), .Q(register_1_q), .clk(clk), .clr(rst));
  assign src2_out = decoder_3_out1 ? register_1_q : 18'bz;  // Controlled_Buffer controlled_buffer_1
  assign src1_out = decoder_2_out1 ? register_1_q : 18'bz;  // Controlled_Buffer controlled_buffer_2
  assign src2_out = decoder_3_out3 ? register_2_q : 18'bz;  // Controlled_Buffer controlled_buffer_3
  Register #(.width(18)) register_2 (.D(\input ), .en(r3), .Q(register_2_q), .clk(clk), .clr(rst));
  assign src1_out = decoder_2_out3 ? register_2_q : 18'bz;  // Controlled_Buffer controlled_buffer_4
  assign src2_out = decoder_3_out5 ? register_3_q : 18'bz;  // Controlled_Buffer controlled_buffer_5
  Register #(.width(18)) register_3 (.D(\input ), .en(r5), .Q(register_3_q), .clk(clk), .clr(rst));
  assign src1_out = decoder_2_out5 ? register_3_q : 18'bz;  // Controlled_Buffer controlled_buffer_6
  assign src2_out = decoder_3_out7 ? register_4_q : 18'bz;  // Controlled_Buffer controlled_buffer_7
  Register #(.width(18)) register_4 (.D(\input ), .en(r7), .Q(register_4_q), .clk(clk), .clr(rst));
  assign src1_out = decoder_2_out7 ? register_4_q : 18'bz;  // Controlled_Buffer controlled_buffer_8
  assign src2_out = decoder_3_out9 ? register_5_q : 18'bz;  // Controlled_Buffer controlled_buffer_9
  Register #(.width(18)) register_5 (.D(\input ), .en(r9), .Q(register_5_q), .clk(clk), .clr(rst));
  assign src1_out = decoder_2_out9 ? register_5_q : 18'bz;  // Controlled_Buffer controlled_buffer_10
  assign src2_out = decoder_3_out11 ? register_6_q : 18'bz;  // Controlled_Buffer controlled_buffer_11
  Register #(.width(18)) register_6 (.D(\input ), .en(r11), .Q(register_6_q), .clk(clk), .clr(rst));
  assign src1_out = decoder_2_out11 ? register_6_q : 18'bz;  // Controlled_Buffer controlled_buffer_12
  Register #(.width(18)) register_7 (.D(\input ), .en(r13), .Q(register_7_q), .clk(clk), .clr(rst));
  assign src2_out = decoder_3_out13 ? register_7_q : 18'bz;  // Controlled_Buffer controlled_buffer_13
  assign src1_out = decoder_2_out13 ? register_7_q : 18'bz;  // Controlled_Buffer controlled_buffer_14
  assign src2_out = decoder_3_out15 ? register_8_q : 18'bz;  // Controlled_Buffer controlled_buffer_15
  Register #(.width(18)) register_8 (.D(\input ), .en(r15), .Q(register_8_q), .clk(clk), .clr(rst));
  assign src1_out = decoder_2_out15 ? register_8_q : 18'bz;  // Controlled_Buffer controlled_buffer_16
  Register #(.width(18)) register_9 (.D(\input ), .en(r0), .Q(register_9_q), .clk(clk), .clr(rst));
  Register #(.width(18)) register_10 (.D(\input ), .en(r2), .Q(register_10_q), .clk(clk), .clr(rst));
  Register #(.width(18)) register_11 (.D(\input ), .en(r4), .Q(register_11_q), .clk(clk), .clr(rst));
  Register #(.width(18)) register_12 (.D(\input ), .en(r6), .Q(register_12_q), .clk(clk), .clr(rst));
  Register #(.width(18)) register_13 (.D(\input ), .en(r8), .Q(register_13_q), .clk(clk), .clr(rst));
  Register #(.width(18)) register_14 (.D(\input ), .en(r10), .Q(register_14_q), .clk(clk), .clr(rst));
  Register #(.width(18)) register_15 (.D(\input ), .en(r12), .Q(register_15_q), .clk(clk), .clr(rst));
  Register #(.width(18)) register_16 (.D(\input ), .en(r14), .Q(register_16_q), .clk(clk), .clr(rst));
  assign src2_out = decoder_3_out0 ? register_9_q : 18'bz;  // Controlled_Buffer controlled_buffer_17
  assign src1_out = decoder_2_out0 ? register_9_q : 18'bz;  // Controlled_Buffer controlled_buffer_18
  assign src2_out = decoder_3_out2 ? register_10_q : 18'bz;  // Controlled_Buffer controlled_buffer_19
  assign src1_out = decoder_2_out2 ? register_10_q : 18'bz;  // Controlled_Buffer controlled_buffer_20
  assign src2_out = decoder_3_out4 ? register_11_q : 18'bz;  // Controlled_Buffer controlled_buffer_21
  assign src1_out = decoder_2_out4 ? register_11_q : 18'bz;  // Controlled_Buffer controlled_buffer_22
  assign src2_out = decoder_3_out6 ? register_12_q : 18'bz;  // Controlled_Buffer controlled_buffer_23
  assign src1_out = decoder_2_out6 ? register_12_q : 18'bz;  // Controlled_Buffer controlled_buffer_24
  assign src2_out = decoder_3_out8 ? register_13_q : 18'bz;  // Controlled_Buffer controlled_buffer_25
  assign src1_out = decoder_2_out8 ? register_13_q : 18'bz;  // Controlled_Buffer controlled_buffer_26
  assign src2_out = decoder_3_out10 ? register_14_q : 18'bz;  // Controlled_Buffer controlled_buffer_27
  assign src1_out = decoder_2_out10 ? register_14_q : 18'bz;  // Controlled_Buffer controlled_buffer_28
  assign src2_out = decoder_3_out12 ? register_15_q : 18'bz;  // Controlled_Buffer controlled_buffer_29
  assign src1_out = decoder_2_out12 ? register_15_q : 18'bz;  // Controlled_Buffer controlled_buffer_30
  assign src2_out = decoder_3_out14 ? register_16_q : 18'bz;  // Controlled_Buffer controlled_buffer_31
  assign src1_out = decoder_2_out14 ? register_16_q : 18'bz;  // Controlled_Buffer controlled_buffer_32
  Decoder #(.select(4), .enable("false")) decoder_3 (
    .out0(decoder_3_out0), .out1(decoder_3_out1), .out2(decoder_3_out2), .out3(decoder_3_out3),
    .out4(decoder_3_out4), .out5(decoder_3_out5), .out6(decoder_3_out6), .out7(decoder_3_out7),
    .out8(decoder_3_out8), .out9(decoder_3_out9), .out10(decoder_3_out10), .out11(decoder_3_out11),
    .out12(decoder_3_out12), .out13(decoder_3_out13), .out14(decoder_3_out14), .out15(decoder_3_out15),
    .sel(src2Adr));

  // Other names for the same wires on the sheet: src1[17:0] = src1_out; src1Addr[3:0] = src1adr;
  //   src2[17:0] = src2_out; src2Addr[3:0] = src2Adr
endmodule

module Half_Adder (
  input  a,
  input  b,
  output s,
  output co
);

  wire and_2_out, and_3_out, not_1_out, not_2_out;

  not not_1 (not_1_out, a);
  not not_2 (not_2_out, b);
  and and_1 (co, a, b);
  and and_2 (and_2_out, not_1_out, b);
  and and_3 (and_3_out, a, not_2_out);
  or or_1 (s, and_2_out, and_3_out);
endmodule

module Full_Adder (
  input  a,
  input  b,
  input  ci,
  output s,
  output co
);

  wire and_1_out, and_2_out, and_3_out, and_4_out, and_5_out, and_6_out, and_7_out;

  and and_1 (and_1_out, b, ci);
  and and_2 (and_2_out, a, ci);
  and and_3 (and_3_out, a, b);
  and and_4 (and_4_out, ~a, ~b, ci);  // AND_Gate
  and and_5 (and_5_out, ~a, b, ~ci);  // AND_Gate
  and and_6 (and_6_out, a, ~b, ~ci);  // AND_Gate
  and and_7 (and_7_out, a, b, ci);
  or or_1 (co, and_1_out, and_2_out, and_3_out);
  or or_2 (s, and_4_out, and_5_out, and_6_out, and_7_out);
endmodule

module _4_Bits_Adder (
  input  [3:0] a,
  input  [3:0] b,
  input  c_in,
  output c_out,
  output [3:0] s
);

  wire full_adder_2_co, full_adder_3_co, full_adder_4_co;

  Full_Adder full_adder_1 (.a(a[3]), .b(b[3]), .ci(full_adder_2_co), .s(s[3]), .co(c_out));
  Full_Adder full_adder_2 (.a(a[2]), .b(b[2]), .ci(full_adder_4_co), .s(s[2]), .co(full_adder_2_co));
  Full_Adder full_adder_3 (.a(a[0]), .b(b[0]), .ci(c_in), .s(s[0]), .co(full_adder_3_co));
  Full_Adder full_adder_4 (.a(a[1]), .b(b[1]), .ci(full_adder_3_co), .s(s[1]), .co(full_adder_4_co));
endmodule

module _18_Bits_Adder (
  input  [17:0] a,
  input  [17:0] b,
  output c_out,
  output [17:0] s
);

  wire full_adder_1_co, half_adder_1_co, n4_bits_adder_1_c_out, n4_bits_adder_3_c_out, n4_bits_adder_4_c_out;

  _4_Bits_Adder u_4_bits_adder_1 (
    .c_in(n4_bits_adder_3_c_out), .a(a[13:10]), .b(b[13:10]), .c_out(n4_bits_adder_1_c_out), .s(s[13:10]));
  _4_Bits_Adder u_4_bits_adder_2 (
    .c_in(n4_bits_adder_1_c_out), .a(a[17:14]), .b(b[17:14]), .c_out(c_out), .s(s[17:14]));
  _4_Bits_Adder u_4_bits_adder_3 (
    .c_in(n4_bits_adder_4_c_out), .a(a[9:6]), .b(b[9:6]), .c_out(n4_bits_adder_3_c_out), .s(s[9:6]));
  _4_Bits_Adder u_4_bits_adder_4 (
    .c_in(full_adder_1_co), .a(a[5:2]), .b(b[5:2]), .c_out(n4_bits_adder_4_c_out), .s(s[5:2]));
  Full_Adder full_adder_1 (.a(a[1]), .b(b[1]), .ci(half_adder_1_co), .s(s[1]), .co(full_adder_1_co));
  Half_Adder half_adder_1 (.a(a[0]), .b(b[0]), .s(s[0]), .co(half_adder_1_co));
endmodule

module _1_Bit_Comparator (
  input  a,
  input  b,
  input  n_in,
  input  z_in,
  input  p_in,
  output n_out,
  output z_out,
  output p_out
);

  wire and_1_out, and_3_out, xnor_1_out;

  and and_1 (and_1_out, z_in, ~a, b);  // AND_Gate
  or or_1 (n_out, and_1_out, n_in);
  xnor xnor_1 (xnor_1_out, a, b);
  and and_2 (z_out, z_in, xnor_1_out);
  and and_3 (and_3_out, z_in, a, ~b);  // AND_Gate
  or or_2 (p_out, p_in, and_3_out);
endmodule

module _4_Bits_Comparator (
  input  [3:0] a,
  input  [3:0] b,
  input  n_in,
  input  z_in,
  input  p_in,
  output n_out,
  output z_out,
  output p_out
);

  wire n1_bit_comparator_1_n_out, n1_bit_comparator_1_p_out, n1_bit_comparator_1_z_out,
       n1_bit_comparator_2_n_out, n1_bit_comparator_2_p_out, n1_bit_comparator_2_z_out,
       n1_bit_comparator_3_n_out, n1_bit_comparator_3_p_out, n1_bit_comparator_3_z_out;

  _1_Bit_Comparator u_1_bit_comparator_1 (
    .n_in(n_in), .z_in(z_in), .p_in(p_in), .a(a[3]), .b(b[3]), .n_out(n1_bit_comparator_1_n_out),
    .z_out(n1_bit_comparator_1_z_out), .p_out(n1_bit_comparator_1_p_out));
  _1_Bit_Comparator u_1_bit_comparator_2 (
    .n_in(n1_bit_comparator_1_n_out), .z_in(n1_bit_comparator_1_z_out), .p_in(n1_bit_comparator_1_p_out),
    .a(a[2]), .b(b[2]), .n_out(n1_bit_comparator_2_n_out), .z_out(n1_bit_comparator_2_z_out),
    .p_out(n1_bit_comparator_2_p_out));
  _1_Bit_Comparator u_1_bit_comparator_3 (
    .n_in(n1_bit_comparator_2_n_out), .z_in(n1_bit_comparator_2_z_out), .p_in(n1_bit_comparator_2_p_out),
    .a(a[1]), .b(b[1]), .n_out(n1_bit_comparator_3_n_out), .z_out(n1_bit_comparator_3_z_out),
    .p_out(n1_bit_comparator_3_p_out));
  _1_Bit_Comparator u_1_bit_comparator_4 (
    .n_in(n1_bit_comparator_3_n_out), .z_in(n1_bit_comparator_3_z_out), .p_in(n1_bit_comparator_3_p_out),
    .a(a[0]), .b(b[0]), .n_out(n_out), .z_out(z_out), .p_out(p_out));
endmodule

module _18_Bits_Comparator (
  input  [17:0] a,
  input  [17:0] b,
  output n_out,
  output z_out,
  output p_out
);

  wire n1_bit_comparator_1_n_out, n1_bit_comparator_1_p_out, n1_bit_comparator_1_z_out,
       n4_bits_comparator_1_n_out, n4_bits_comparator_1_p_out, n4_bits_comparator_1_z_out,
       n4_bits_comparator_2_n_out, n4_bits_comparator_2_p_out, n4_bits_comparator_2_z_out,
       n4_bits_comparator_3_n_out, n4_bits_comparator_3_p_out, n4_bits_comparator_3_z_out,
       n4_bits_comparator_4_n_out, n4_bits_comparator_4_p_out, n4_bits_comparator_4_z_out;

  _4_Bits_Comparator u_4_bits_comparator_1 (
    .n_in(1'b0), .z_in(1'b1), .p_in(1'b0), .n_out(n4_bits_comparator_1_n_out),
    .z_out(n4_bits_comparator_1_z_out), .p_out(n4_bits_comparator_1_p_out), .a(a[17:14]), .b(b[17:14]));
  _4_Bits_Comparator u_4_bits_comparator_2 (
    .n_in(n4_bits_comparator_1_n_out), .z_in(n4_bits_comparator_1_z_out), .p_in(n4_bits_comparator_1_p_out),
    .n_out(n4_bits_comparator_2_n_out), .z_out(n4_bits_comparator_2_z_out),
    .p_out(n4_bits_comparator_2_p_out), .a(a[13:10]), .b(b[13:10]));
  _4_Bits_Comparator u_4_bits_comparator_3 (
    .n_in(n4_bits_comparator_4_n_out), .z_in(n4_bits_comparator_4_z_out), .p_in(n4_bits_comparator_4_p_out),
    .n_out(n4_bits_comparator_3_n_out), .z_out(n4_bits_comparator_3_z_out),
    .p_out(n4_bits_comparator_3_p_out), .a(a[5:2]), .b(b[5:2]));
  _4_Bits_Comparator u_4_bits_comparator_4 (
    .n_in(n4_bits_comparator_2_n_out), .z_in(n4_bits_comparator_2_z_out), .p_in(n4_bits_comparator_2_p_out),
    .n_out(n4_bits_comparator_4_n_out), .z_out(n4_bits_comparator_4_z_out),
    .p_out(n4_bits_comparator_4_p_out), .a(a[9:6]), .b(b[9:6]));
  _1_Bit_Comparator u_1_bit_comparator_1 (
    .n_in(n4_bits_comparator_3_n_out), .z_in(n4_bits_comparator_3_z_out), .p_in(n4_bits_comparator_3_p_out),
    .a(a[1]), .b(b[1]), .n_out(n1_bit_comparator_1_n_out), .z_out(n1_bit_comparator_1_z_out),
    .p_out(n1_bit_comparator_1_p_out));
  _1_Bit_Comparator u_1_bit_comparator_2 (
    .n_in(n1_bit_comparator_1_n_out), .z_in(n1_bit_comparator_1_z_out), .p_in(n1_bit_comparator_1_p_out),
    .a(a[0]), .b(b[0]), .n_out(n_out), .z_out(z_out), .p_out(p_out));
endmodule

module _1_Bit_Logic_Unit (
  input  forAdderBit,
  input  a,
  input  b,
  input  [1:0] s,
  output r
);

  wire and_1_out, or_1_out, xor_1_out;

  and and_1 (and_1_out, b, a);
  or or_1 (or_1_out, b, a);
  xor xor_1 (xor_1_out, b, a);
  Multiplexer #(.select(2), .enable("false")) multiplexer_1 (
    .in0(forAdderBit), .in1(and_1_out), .in2(or_1_out), .in3(xor_1_out), .out(r), .sel(s));
endmodule

module _4_Bits_Logic_Unit (
  input  [3:0] forAdderBits,
  input  [3:0] a,
  input  [3:0] b,
  input  [1:0] s,
  output [3:0] r
);

  _1_Bit_Logic_Unit u_1_bit_logic_unit_1 (.r(r[3]), .a(a[3]), .b(b[3]), .s(s), .forAdderBit(forAdderBits[3]));
  _1_Bit_Logic_Unit u_1_bit_logic_unit_2 (.r(r[2]), .a(a[2]), .b(b[2]), .s(s), .forAdderBit(forAdderBits[2]));
  _1_Bit_Logic_Unit u_1_bit_logic_unit_3 (.r(r[1]), .a(a[1]), .b(b[1]), .s(s), .forAdderBit(forAdderBits[1]));
  _1_Bit_Logic_Unit u_1_bit_logic_unit_4 (.r(r[0]), .a(a[0]), .b(b[0]), .s(s), .forAdderBit(forAdderBits[0]));
endmodule

module _18_Bits_Logic_Unit (
  input  [17:0] forAdderBits,
  input  [17:0] a,
  input  [17:0] b,
  input  [1:0] s,
  output [17:0] r
);

  _4_Bits_Logic_Unit u_4_bits_logic_unit_1 (
    .s(s), .a(a[17:14]), .b(b[17:14]), .r(r[17:14]), .forAdderBits(forAdderBits[17:14]));
  _4_Bits_Logic_Unit u_4_bits_logic_unit_2 (
    .s(s), .a(a[13:10]), .b(b[13:10]), .r(r[13:10]), .forAdderBits(forAdderBits[13:10]));
  _4_Bits_Logic_Unit u_4_bits_logic_unit_3 (
    .s(s), .a(a[9:6]), .b(b[9:6]), .r(r[9:6]), .forAdderBits(forAdderBits[9:6]));
  _4_Bits_Logic_Unit u_4_bits_logic_unit_4 (
    .s(s), .a(a[5:2]), .b(b[5:2]), .r(r[5:2]), .forAdderBits(forAdderBits[5:2]));
  _1_Bit_Logic_Unit u_1_bit_logic_unit_1 (.r(r[0]), .a(a[0]), .b(b[0]), .s(s), .forAdderBit(forAdderBits[0]));
  _1_Bit_Logic_Unit u_1_bit_logic_unit_2 (.r(r[1]), .a(a[1]), .b(b[1]), .s(s), .forAdderBit(forAdderBits[1]));
endmodule

module Arithmetic_Logic_Unit (
  input  [17:0] a,
  input  [17:0] b,
  input  [1:0] s,
  output [17:0] r
);

  wire [17:0] n18_bits_adder_1_s;

  _18_Bits_Adder u_18_bits_adder_1 (.a(a), .b(b), .s(n18_bits_adder_1_s));  // open: c_out
  _18_Bits_Logic_Unit u_18_bits_logic_unit_1 (.s(s), .a(a), .b(b), .r(r), .forAdderBits(n18_bits_adder_1_s));
endmodule

module Control_Unit (
  input  [17:0] Instruction,
  input  clk,
  input  [17:0] opInput1,
  input  [17:0] opIntput2,
  output IRW,
  output PCW,
  output [9:0] loadAddrress,
  output [13:0] jumpAddrress,
  output [5:0] branchAddress,
  output [1:0] ALUSelectionBits,
  output isJump,
  output [3:0] dstAddr,
  output [3:0] src1Addr,
  output [3:0] src2Addr,
  output isLoad,
  output isStore,
  output [5:0] immValue,
  output isBranch,
  output isImmediate,
  output isRegisterWritable,
  output branchSignal
);

  wire ADD, ADDI, AND, and_1_out, and_2_out, and_3_out, and_4_out, and_5_out, ANDI, BEQ, BGE, BGT, BLE, BLT,
       n, not_2_out, OR, ORI, p, XOR, XORI, z;

  or or_1 (isImmediate, ADDI, ANDI, ORI, XORI);
  or or_2 (isRegisterWritable, ADD, ADDI, AND, ANDI, OR, ORI, XOR, XORI);
  or or_3 (isBranch, BEQ, BLT, BGT, BLE, BGE);
  _18_Bits_Comparator u_18_bits_comparator_1 (.n_out(n), .z_out(z), .p_out(p), .a(opInput1), .b(opIntput2));
  and and_1 (and_1_out, z, BEQ);
  and and_2 (and_2_out, n, BLT);
  and and_3 (and_3_out, p, BGT);
  and and_4 (and_4_out, z, n, BLE);
  and and_5 (and_5_out, p, z, BGE);
  or or_4 (branchSignal, and_1_out, and_2_out, and_3_out, and_4_out, and_5_out);
  not not_1 (IRW, PCW);
  Decoder #(.select(4), .enable("false")) decoder_1 (
    .out0(ADD), .out1(ADDI), .out2(AND), .out3(ANDI), .out4(OR), .out5(ORI), .out6(XOR), .out7(XORI),
    .out8(isJump), .out9(isLoad), .out10(isStore), .out11(BEQ), .out12(BLT), .out13(BGT), .out14(BLE),
    .out15(BGE), .sel(Instruction[17:14]));
  D_Flip_Flop d_ff_1 (.clk(clk), .D(not_2_out), .Q(PCW));  // open: Qn, preset, en, reset
  not not_2 (not_2_out, PCW);

  assign ALUSelectionBits = Instruction[16:15];
  assign branchAddress = Instruction[5:0];
  assign dstAddr = Instruction[13:10];
  assign immValue = Instruction[5:0];
  assign jumpAddrress = Instruction[13:0];
  assign loadAddrress = Instruction[9:0];
  assign src1Addr = Instruction[9:6];
  assign src2Addr = Instruction[5:2];

  // Other names for the same wires on the sheet: dstAddress[3:0] = Instruction[13:10];
  //   src2Address[3:0] = Instruction[5:2]; JUMP = isJump; LOAD = isLoad; opCode[3:0] = Instruction[17:14];
  //   src1Address[3:0] = Instruction[9:6]; state = PCW; STORE = isStore
endmodule

module Program_Counter (
  input  [13:0] jumpAddr,
  input  [5:0] branchAddr,
  input  isJump,
  input  isBranch,
  input  clk,
  input  write_enabled,
  input  rst,
  output [9:0] instructionAddress
);

  wire n18_bits_adder_1_c_out, n18_bits_adder_2_c_out, or_1_out;
  wire [17:0] multiplexer_1_out, multiplexer_2_out, n6x18bits_extension_1_output,
       n14x18_bits_extension_1_output, n18_bits_adder_1_s, n18_bits_adder_2_s, register_1_q;

  _14x18_Bits_Extension u_14x18_bits_extension_1 (
    .in_2(1'b1), .\output (n14x18_bits_extension_1_output), .\input (jumpAddr));
  _6x18Bits_Extension u_6x18bits_extension_1 (
    .\output (n6x18bits_extension_1_output), .\input (branchAddr), .in_2(1'b1));
  or or_1 (or_1_out, isJump, isBranch);
  _18_Bits_Adder u_18_bits_adder_1 (
    .a(multiplexer_2_out), .b(register_1_q), .c_out(n18_bits_adder_1_c_out), .s(n18_bits_adder_1_s));
  // Probe on multiplexer_1_out
  Multiplexer #(.width(18), .enable("false")) multiplexer_1 (
    .in0(n14x18_bits_extension_1_output), .in1(n6x18bits_extension_1_output), .out(multiplexer_1_out),
    .sel(isBranch));
  Multiplexer #(.width(18), .enable("false")) multiplexer_2 (
    .in0(18'h1), .in1(n18_bits_adder_2_s), .out(multiplexer_2_out), .sel(or_1_out));
  Register #(.width(18)) register_1 (
    .D(n18_bits_adder_1_s), .en(write_enabled), .Q(register_1_q), .clk(clk), .clr(rst));
  _18_Bits_Adder u_18_bits_adder_2 (
    .a(18'h1), .b(multiplexer_1_out), .c_out(n18_bits_adder_2_c_out), .s(n18_bits_adder_2_s));
  _18x10_Bits_Extension u_18x10_bits_extension_1 (.\output (instructionAddress), .\input (register_1_q));
endmodule

module _6x18Bits_Extension (
  input  [5:0] \input ,
  input  in_2,
  output [17:0] \output 
);

  wire multiplexer_1_out;

  Multiplexer #(.enable("false")) multiplexer_1 (.in0(1'b0), .in1(\input [5]), .out(multiplexer_1_out), .sel(in_2));
  Multiplexer #(.width(12), .enable("false")) multiplexer_2 (
    .in0({12{1'b0}}), .in1({12{1'b1}}), .out(\output [17:6]), .sel(multiplexer_1_out));

  assign \output [5:0] = \input ;
endmodule

module _14x18_Bits_Extension (
  input  [13:0] \input ,
  input  in_2,
  output [17:0] \output 
);

  wire multiplexer_1_out;

  Multiplexer #(.enable("false")) multiplexer_1 (.in0(1'b0), .in1(\input [13]), .out(multiplexer_1_out), .sel(in_2));
  Multiplexer #(.width(4), .enable("false")) multiplexer_2 (
    .in0(4'b0000), .in1(4'b1111), .out(\output [17:14]), .sel(multiplexer_1_out));

  assign \output [13:0] = \input ;
endmodule

module _18x10_Bits_Extension (
  input  [17:0] \input ,
  output [9:0] \output 
);


  assign \output  = \input [9:0];
endmodule
